// Digital circuit frontpanel.dig as structural Verilog
module frontpanel (
  input  [15:0] value,
  input  [1:0] dest,
  input  [1:0] src,
  output [15:0] R0,
  output [15:0] R1,
  output [15:0] R2,
  output [15:0] R3,
  output [15:0] B,
  output [1:0] rs,
  output [1:0] rd,
  output [15:0] A
);

  wire add_out, assembler_1_store_clk, button_1_out, execute_1_p3, jump_out, mode_out;
  wire [1:0] PC_out;
  wire [31:0] assembler_1_inst, Program_d;

  LED programming (.in(mode_out));
  DipSwitch mode (.out(mode_out));
  Button add (.out(add_out));
  Button jump (.out(jump_out));
  assembler assembler_1 (
    .mode(mode_out), .value(value), .dest(dest), .src(src), .add(add_out), .jump(jump_out),
    .inst(assembler_1_inst), .store_clk(assembler_1_store_clk));
  Counter #(.Bits(2)) PC (.en(1'b1), .C(button_1_out), .clr(1'b0), .out(PC_out));  // open: ovf
  Button button_1 (.out(button_1_out));
  EEPROMDualPort #(.isProgramMemory("true"), .Bits(32)) Program (
    .A(PC_out), .Din(assembler_1_inst), .str(1'b1), .C(assembler_1_store_clk), .ld(1'b1), .D(Program_d));
  // decoder decoder_1: pin names not known; wires that end beside it: mode_out, assembler_1_inst, Program_d, A, rs, rd
  // execute execute_1: pin names not known; wires that end beside it: A, B, execute_1_p3
  // regfile regfile_1: pin names not known; wires that end beside it: rs, rd, execute_1_p3, button_1_out, B, R0, R1, R2, R3

  // Notes on the sheet:
  //   contents of Program (hex, n*v repeats v):
  //   10064,1200c8,230063,300022
  //   R
  //   =
  //   +
  //   ( R
  //   )
endmodule
